// Logisim project 16-Bit Adder.circ as structural Verilog: 1 circuit, main circuit 16-Bit Adder
module _16_Bit_Adder (
  input  [15:0] A,
  input  [15:0] B,
  input  Cin,
  output Cout,
  output [15:0] Sum
);

  wire full_adder_1_cout, full_adder_2_cout, full_adder_3_cout, full_adder_4_cout, full_adder_5_cout,
       full_adder_6_cout, full_adder_7_cout, full_adder_8_cout, full_adder_9_cout, full_adder_10_cout,
       full_adder_11_cout, full_adder_12_cout, full_adder_13_cout, full_adder_14_cout, full_adder_15_cout;

  Full_Adder full_adder_1 (.A(A[0]), .B(B[0]), .Cin(Cin), .Sum(Sum[0]), .Cout(full_adder_1_cout));
  Full_Adder full_adder_2 (.A(A[1]), .B(B[1]), .Cin(full_adder_1_cout), .Sum(Sum[1]), .Cout(full_adder_2_cout));
  Full_Adder full_adder_3 (.A(A[2]), .B(B[2]), .Cin(full_adder_2_cout), .Sum(Sum[2]), .Cout(full_adder_3_cout));
  Full_Adder full_adder_4 (.A(A[3]), .B(B[3]), .Cin(full_adder_3_cout), .Sum(Sum[3]), .Cout(full_adder_4_cout));
  Full_Adder full_adder_5 (.A(A[4]), .B(B[4]), .Cin(full_adder_4_cout), .Sum(Sum[4]), .Cout(full_adder_5_cout));
  Full_Adder full_adder_6 (.A(A[5]), .B(B[5]), .Cin(full_adder_5_cout), .Sum(Sum[5]), .Cout(full_adder_6_cout));
  Full_Adder full_adder_7 (.A(A[6]), .B(B[6]), .Cin(full_adder_6_cout), .Sum(Sum[6]), .Cout(full_adder_7_cout));
  Full_Adder full_adder_8 (.A(A[7]), .B(B[7]), .Cin(full_adder_7_cout), .Sum(Sum[7]), .Cout(full_adder_8_cout));
  Full_Adder full_adder_9 (.A(A[8]), .B(B[8]), .Cin(full_adder_8_cout), .Sum(Sum[8]), .Cout(full_adder_9_cout));
  Full_Adder full_adder_10 (.A(A[9]), .B(B[9]), .Cin(full_adder_9_cout), .Sum(Sum[9]), .Cout(full_adder_10_cout));
  Full_Adder full_adder_11 (.A(A[10]), .B(B[10]), .Cin(full_adder_10_cout), .Sum(Sum[10]), .Cout(full_adder_11_cout));
  Full_Adder full_adder_12 (.A(A[11]), .B(B[11]), .Cin(full_adder_11_cout), .Sum(Sum[11]), .Cout(full_adder_12_cout));
  Full_Adder full_adder_13 (.A(A[12]), .B(B[12]), .Cin(full_adder_12_cout), .Sum(Sum[12]), .Cout(full_adder_13_cout));
  Full_Adder full_adder_14 (.A(A[13]), .B(B[13]), .Cin(full_adder_13_cout), .Sum(Sum[13]), .Cout(full_adder_14_cout));
  Full_Adder full_adder_15 (.A(A[14]), .B(B[14]), .Cin(full_adder_14_cout), .Sum(Sum[14]), .Cout(full_adder_15_cout));
  Full_Adder full_adder_16 (.A(A[15]), .B(B[15]), .Cin(full_adder_15_cout), .Sum(Sum[15]), .Cout(Cout));

  // Notes on the sheet:
  //   Hakan Şahin - 64355 / Yasemin Melek - 63929
endmodule
