// Logisim project ALU.circ as structural Verilog: 1 circuit, main circuit ALU
module ALU (
  input  [15:0] A,
  input  [15:0] B,
  input  [4:0] SHAMT,
  input  [5:0] OPCODE,
  input  CLK,
  output [15:0] ALUResult,
  output Zero,
  output Cout,
  output Overflow
);

  wire and_2_out, and_3_out, and_4_out, and_5_out, comparator_1_lt, comparator_2_eq, n16_bit_adder_1_cout,
       n16_bit_adder_2_cout, not_1_out, not_2_out, subtractor_1_bout, xor_1_out, xor_2_out, xor_3_out,
       xor_4_out, xor_5_out, xor_6_out;
  wire [15:0] ADD_RESULT, ADDI_RESULT, and_1_out, bit_extender_1_out, divider_1_rem, hi_q, lo_q,
       multiplier_1_cout, multiplier_1_out, or_1_out, shifter_1_out, SUB_RESULT;

  _16_Bit_Adder u_16_bit_adder_1 (.A(A), .B(B), .Cin(1'b0), .Cout(n16_bit_adder_1_cout), .Sum(ADD_RESULT));
  Subtractor #(.width(16)) subtractor_1 (.a(A), .b(B), .out(SUB_RESULT), .bout(subtractor_1_bout));  // open: bin
  Multiplier #(.width(16)) multiplier_1 (.a(A), .b(B), .out(multiplier_1_out), .cout(multiplier_1_cout));  // open: cin
  assign and_1_out = A & B;  // AND_Gate and_1, 16 bits wide
  assign or_1_out = A | B;  // OR_Gate or_1, 16 bits wide
  _16_Bit_Adder u_16_bit_adder_2 (.A(A), .B(B), .Cin(1'b0), .Cout(n16_bit_adder_2_cout), .Sum(ADDI_RESULT));
  Shifter #(.width(16)) shifter_1 (.in(A), .\dist (SHAMT[3:0]), .out(shifter_1_out));
  Comparator #(.width(16)) comparator_1 (.a(A), .b(B), .lt(comparator_1_lt));  // open: gt, eq
  Divider #(.width(16)) divider_1 (.a(A), .b(B), .rem(divider_1_rem));  // open: out, upper
  xor xor_1 (xor_1_out, A[15], ADD_RESULT[15]);
  xor xor_2 (xor_2_out, B[15], ADD_RESULT[15]);
  xor xor_3 (xor_3_out, A[15], SUB_RESULT[15]);
  xor xor_4 (xor_4_out, B[15], SUB_RESULT[15]);
  xor xor_5 (xor_5_out, A[15], ADDI_RESULT[15]);
  xor xor_6 (xor_6_out, B[15], ADDI_RESULT[15]);
  assign bit_extender_1_out = {{15{1'b0}}, comparator_1_lt};  // Bit_Extender bit_extender_1
  and and_2 (and_2_out, xor_1_out, xor_2_out);
  and and_3 (and_3_out, xor_3_out, xor_4_out);
  and and_4 (and_4_out, xor_5_out, xor_6_out);
  Multiplexer #(.select(4), .width(16)) multiplexer_1 (
    .in0(ADD_RESULT), .in1(SUB_RESULT), .in3(and_1_out), .in4(or_1_out), .in5(ADDI_RESULT),
    .in6(shifter_1_out), .in7(bit_extender_1_out), .in8(hi_q), .in9(lo_q), .in15(divider_1_rem),
    .out(ALUResult), .sel(OPCODE[3:0]), .en(and_5_out));  // open: in2, in10, in11, in12, in13, in14
  and and_5 (and_5_out, not_2_out, not_1_out);
  not not_1 (not_1_out, OPCODE[5]);
  not not_2 (not_2_out, OPCODE[4]);
  Comparator #(.width(4)) comparator_2 (.a(OPCODE[3:0]), .b(4'b0010), .eq(comparator_2_eq));  // open: gt, lt
  Multiplexer #(.select(4)) multiplexer_2 (
    .in0(n16_bit_adder_1_cout), .in1(subtractor_1_bout), .in5(n16_bit_adder_2_cout), .out(Cout),
    .sel(OPCODE[3:0]), .en(and_5_out));  // open: in2, in3, in4, in6, in7, in8, in9, in10, in11, in12, in13, in14, in15
  Multiplexer #(.select(4)) multiplexer_3 (
    .in0(and_2_out), .in1(and_3_out), .in5(and_4_out), .out(Overflow), .sel(OPCODE[3:0]), .en(and_5_out));  // open: in2, in3, in4, in6, in7, in8, in9, in10, in11, in12, in13, in14, in15
  Register #(.width(16)) lo (.D(multiplier_1_out), .en(comparator_2_eq), .Q(lo_q), .clk(CLK));  // open: clr
  Register #(.width(16)) hi (.D(multiplier_1_cout), .en(comparator_2_eq), .Q(hi_q), .clk(CLK));  // open: clr
  Comparator #(.width(16)) comparator_3 (.a(ALUResult), .b({16{1'b0}}), .eq(Zero));  // open: gt, lt

  // Notes on the sheet:
  //   Hakan Şahin - 64355 / Yasemin Melek - 63929
endmodule
