// Logisim project Control Unit.circ as structural Verilog: 1 circuit, main circuit Control Unit
module Control_Unit (
  input  [5:0] Opcode,
  output RegDst,
  output ALUSrc,
  output MemtoReg,
  output RegWrite,
  output MemRead,
  output MemWrite,
  output Branch,
  output Jump,
  output [5:0] ALUOp
);

  wire and_1_out, comparator_1_eq, comparator_2_eq, comparator_3_eq, comparator_4_eq, comparator_5_eq,
       comparator_6_eq, comparator_7_eq, comparator_8_eq, comparator_9_eq, comparator_10_eq,
       comparator_13_eq, comparator_14_eq, comparator_16_eq;

  Multiplexer #(.select(4), .width(6)) multiplexer_1 (
    .in0(Opcode), .in1(Opcode), .in2(Opcode), .in3(Opcode), .in4(Opcode), .in5(Opcode), .in6(Opcode),
    .in7(Opcode), .in8(Opcode), .in9(Opcode), .in10({6{1'b0}}), .in11({6{1'b0}}), .in12(6'b000001),
    .in15(Opcode), .out(ALUOp), .sel(Opcode[3:0]), .en(and_1_out));  // open: in13, in14
  and and_1 (and_1_out, ~Opcode[4], ~Opcode[5]);  // AND_Gate
  Comparator #(.width(6)) comparator_1 (.a(Opcode), .b({6{1'b0}}), .eq(comparator_1_eq));  // open: gt, lt
  Comparator #(.width(6)) comparator_2 (.a(Opcode), .b(6'b000001), .eq(comparator_2_eq));  // open: gt, lt
  Comparator #(.width(6)) comparator_3 (.a(Opcode), .b(6'b000010), .eq(comparator_3_eq));  // open: gt, lt
  Comparator #(.width(6)) comparator_4 (.a(Opcode), .b(6'b000011), .eq(comparator_4_eq));  // open: gt, lt
  Comparator #(.width(6)) comparator_5 (.a(Opcode), .b(6'b000100), .eq(comparator_5_eq));  // open: gt, lt
  Comparator #(.width(6)) comparator_6 (.a(Opcode), .b(6'b000101), .eq(comparator_6_eq));  // open: gt, lt
  Comparator #(.width(6)) comparator_7 (.a(Opcode), .b(6'b000110), .eq(comparator_7_eq));  // open: gt, lt
  Comparator #(.width(6)) comparator_8 (.a(Opcode), .b(6'b000111), .eq(comparator_8_eq));  // open: gt, lt
  Comparator #(.width(6)) comparator_9 (.a(Opcode), .b(6'b001000), .eq(comparator_9_eq));  // open: gt, lt
  Comparator #(.width(6)) comparator_10 (.a(Opcode), .b(6'b001001), .eq(comparator_10_eq));  // open: gt, lt
  Comparator #(.width(6)) comparator_11 (.a(Opcode), .b(6'b001010), .eq(MemRead));  // open: gt, lt
  Comparator #(.width(6)) comparator_12 (.a(Opcode), .b(6'b001011), .eq(MemWrite));  // open: gt, lt
  Comparator #(.width(6)) comparator_13 (.a(Opcode), .b(6'b001100), .eq(comparator_13_eq));  // open: gt, lt
  Comparator #(.width(6)) comparator_14 (.a(Opcode), .b(6'b001101), .eq(comparator_14_eq));  // open: gt, lt
  Comparator #(.width(6)) comparator_15 (.a(Opcode), .b(6'b001110), .eq(Jump));  // open: gt, lt
  Comparator #(.width(6)) comparator_16 (.a(Opcode), .b(6'b001111), .eq(comparator_16_eq));  // open: gt, lt
  or or_1 (RegDst, comparator_1_eq, comparator_2_eq, comparator_4_eq, comparator_16_eq, comparator_5_eq, comparator_7_eq, comparator_8_eq);
  or or_2 (ALUSrc, comparator_6_eq, MemRead, MemWrite, comparator_14_eq);
  or or_3 (RegWrite, comparator_1_eq, comparator_2_eq, comparator_4_eq, comparator_5_eq, comparator_6_eq, comparator_8_eq, comparator_9_eq, comparator_10_eq, MemRead, comparator_7_eq, comparator_16_eq);
  or or_4 (Branch, comparator_3_eq, comparator_13_eq, comparator_14_eq);

  assign MemtoReg = MemRead;

  // Other names for the same wires on the sheet: op[5:0] = Opcode

  // Notes on the sheet:
  //   Hakan Şahin - 64355 / Yasemin Melek - 63929
endmodule
