// Logisim project Instruction Splitter.circ as structural Verilog: 1 circuit, main circuit Instruction Splitter
module Instruction_Splitter (
  input  [31:0] Ins,
  output [5:0] OPCODE,
  output [4:0] rs,
  output [4:0] rt,
  output [4:0] rd,
  output [4:0] SHAMT,
  output [5:0] funct,
  output [15:0] IMMEDIATE
);


  assign funct = Ins[5:0];
  assign IMMEDIATE = Ins[15:0];
  assign OPCODE = Ins[31:26];
  assign rd = Ins[15:11];
  assign rs = Ins[25:21];
  assign rt = Ins[20:16];
  assign SHAMT = Ins[10:6];

  // Notes on the sheet:
  //   Hakan Şahin - 64355 / Yasemin Melek - 63929
endmodule
