// Logisim project Register File.circ as structural Verilog: 1 circuit, main circuit Register File
module Register_File (
  input  WControl,
  input  [4:0] src1_addr,
  input  [4:0] dst_addr,
  input  [15:0] Write_Data,
  input  CLK,
  input  [4:0] src2_addr,
  output [15:0] src1_data,
  output [15:0] src2_data
);

  wire _0, _1, _2, _3, _4, _5, _6, _7, _8, _9, _10, _11, _12, _13, _14, _15, and_1_out, and_2_out, and_3_out,
       and_4_out, and_5_out, and_6_out, and_7_out, and_8_out, and_9_out, and_10_out, and_11_out, and_12_out,
       and_13_out, and_14_out, and_15_out, and_16_out, not_1_out, not_2_out, not_3_out;
  wire [15:0] O0, O1, O2, O3, O4, O5, O6, O7, O8, O9, O10, O11, O12, O13, O14, O15;

  not not_1 (not_1_out, dst_addr[4]);
  Decoder #(.select(4)) decoder_1 (
    .out0(_0), .out1(_1), .out2(_2), .out3(_3), .out4(_4), .out5(_5), .out6(_6), .out7(_7), .out8(_8),
    .out9(_9), .out10(_10), .out11(_11), .out12(_12), .out13(_13), .out14(_14), .out15(_15),
    .sel(dst_addr[3:0]), .en(not_1_out));
  and and_1 (and_1_out, _0, WControl);
  and and_2 (and_2_out, _1, WControl);
  and and_3 (and_3_out, _2, WControl);
  and and_4 (and_4_out, _3, WControl);
  and and_5 (and_5_out, _4, WControl);
  and and_6 (and_6_out, _5, WControl);
  and and_7 (and_7_out, _6, WControl);
  and and_8 (and_8_out, _7, WControl);
  Register #(.width(16)) register_1 (.D(Write_Data), .en(and_1_out), .Q(O0), .clk(CLK));  // open: clr
  Register #(.width(16)) register_2 (.D(Write_Data), .en(and_2_out), .Q(O1), .clk(CLK));  // open: clr
  Register #(.width(16)) register_3 (.D(Write_Data), .en(and_3_out), .Q(O2), .clk(CLK));  // open: clr
  Register #(.width(16)) register_4 (.D(Write_Data), .en(and_4_out), .Q(O3), .clk(CLK));  // open: clr
  Register #(.width(16)) register_5 (.D(Write_Data), .en(and_5_out), .Q(O4), .clk(CLK));  // open: clr
  Register #(.width(16)) register_6 (.D(Write_Data), .en(and_6_out), .Q(O5), .clk(CLK));  // open: clr
  Register #(.width(16)) register_7 (.D(Write_Data), .en(and_7_out), .Q(O6), .clk(CLK));  // open: clr
  Register #(.width(16)) register_8 (.D(Write_Data), .en(and_8_out), .Q(O7), .clk(CLK));  // open: clr
  and and_9 (and_9_out, _8, WControl);
  and and_10 (and_10_out, _9, WControl);
  and and_11 (and_11_out, _10, WControl);
  and and_12 (and_12_out, _11, WControl);
  and and_13 (and_13_out, _12, WControl);
  and and_14 (and_14_out, _13, WControl);
  and and_15 (and_15_out, _14, WControl);
  and and_16 (and_16_out, _15, WControl);
  Register #(.width(16)) register_9 (.D(Write_Data), .en(and_9_out), .Q(O8), .clk(CLK));  // open: clr
  Register #(.width(16)) register_10 (.D(Write_Data), .en(and_10_out), .Q(O9), .clk(CLK));  // open: clr
  Register #(.width(16)) register_11 (.D(Write_Data), .en(and_11_out), .Q(O10), .clk(CLK));  // open: clr
  Register #(.width(16)) register_12 (.D(Write_Data), .en(and_12_out), .Q(O11), .clk(CLK));  // open: clr
  Register #(.width(16)) register_13 (.D(Write_Data), .en(and_13_out), .Q(O12), .clk(CLK));  // open: clr
  Register #(.width(16)) register_14 (.D(Write_Data), .en(and_14_out), .Q(O13), .clk(CLK));  // open: clr
  Register #(.width(16)) register_15 (.D(Write_Data), .en(and_15_out), .Q(O14), .clk(CLK));  // open: clr
  Register #(.width(16)) register_16 (.D(Write_Data), .en(and_16_out), .Q(O15), .clk(CLK));  // open: clr
  Multiplexer #(.select(4), .width(16)) multiplexer_1 (
    .in0(O0), .in1(O1), .in2(O2), .in3(O3), .in4(O4), .in5(O5), .in6(O6), .in7(O7), .in8(O8), .in9(O9),
    .in10(O10), .in11(O11), .in12(O12), .in13(O13), .in14(O14), .in15(O15), .out(src1_data),
    .sel(src1_addr[3:0]), .en(not_2_out));
  not not_2 (not_2_out, src1_addr[4]);
  Multiplexer #(.select(4), .width(16)) multiplexer_2 (
    .in0(O0), .in1(O1), .in2(O2), .in3(O3), .in4(O4), .in5(O5), .in6(O6), .in7(O7), .in8(O8), .in9(O9),
    .in10(O10), .in11(O11), .in12(O12), .in13(O13), .in14(O14), .in15(O15), .out(src2_data),
    .sel(src2_addr[3:0]), .en(not_3_out));
  not not_3 (not_3_out, src2_addr[4]);

  // Other names for the same wires on the sheet: WData[15:0] = Write_Data

  // Notes on the sheet:
  //   Hakan Şahin - 64355 / Yasemin Melek - 63929
endmodule
