// Logisim project Single Cycle Processor.circ as structural Verilog: 1 circuit, main circuit Single Cycle Processor
module Single_Cycle_Processor (
);

  wire AluSrc, and_1_out, Branch, button_1_out, button_2_out, CLK, Jump, MemRead, MemtoReg, MemWrite, RegDst,
       RegWrite, Zero;
  wire [4:0] instruction_splitter_1_rd, instruction_splitter_1_rs, instruction_splitter_1_rt,
       multiplexer_2_out, SHAMT;
  wire [5:0] ALUOp, instruction_splitter_1_opcode;
  wire [15:0] alu_1_aluresult, counter_1_q, Immediate, multiplexer_1_out, multiplexer_3_out,
       multiplexer_4_out, multiplexer_5_out, n16_bit_adder_1_sum, n16_bit_adder_2_sum, ram_1_data,
       register_file_1_src1_data, register_file_1_src2_data;
  wire [31:0] rom_1_data;

  Counter #(.width(16)) counter_1 (
    .load(1'b1), .D(multiplexer_3_out), .count(1'b0), .Q(counter_1_q), .clk(CLK), .clr(button_1_out));  // open: carry
  Button button_1 (.out(button_1_out));
  _16_Bit_Adder u_16_bit_adder_1 (.A(16'h1), .B(counter_1_q), .Cin(1'b0), .Sum(n16_bit_adder_1_sum));  // open: Cout
  Clock clock_1 (.out(CLK));
  _16_Bit_Adder u_16_bit_adder_2 (
    .A(n16_bit_adder_1_sum), .B(Immediate), .Cin(1'b0), .Sum(n16_bit_adder_2_sum));  // open: Cout
  ROM #(.addrWidth(16), .dataWidth(32)) rom_1 (.addr(counter_1_q), .data(rom_1_data));  // open: sel
  and and_1 (and_1_out, Branch, Zero);
  Multiplexer #(.width(16), .enable("false")) multiplexer_1 (
    .in0(n16_bit_adder_1_sum), .in1(n16_bit_adder_2_sum), .out(multiplexer_1_out), .sel(and_1_out));
  Instruction_Splitter instruction_splitter_1 (
    .Ins(rom_1_data), .OPCODE(instruction_splitter_1_opcode), .rs(instruction_splitter_1_rs),
    .rt(instruction_splitter_1_rt), .rd(instruction_splitter_1_rd), .SHAMT(SHAMT), .IMMEDIATE(Immediate));  // open: funct
  Control_Unit control_unit_1 (
    .Opcode(instruction_splitter_1_opcode), .RegDst(RegDst), .ALUSrc(AluSrc), .MemtoReg(MemtoReg),
    .RegWrite(RegWrite), .MemRead(MemRead), .MemWrite(MemWrite), .Branch(Branch), .Jump(Jump), .ALUOp(ALUOp));
  Multiplexer #(.width(5), .enable("false")) multiplexer_2 (
    .in0(instruction_splitter_1_rt), .in1(instruction_splitter_1_rd), .out(multiplexer_2_out), .sel(RegDst));
  Multiplexer #(.width(16), .enable("false")) multiplexer_3 (
    .in0(multiplexer_1_out), .in1(Immediate), .out(multiplexer_3_out), .sel(Jump));
  Register_File register_file_1 (
    .WControl(RegWrite), .Write_Data(multiplexer_5_out), .CLK(CLK), .src1_data(register_file_1_src1_data),
    .src2_data(register_file_1_src2_data), .dst_addr(multiplexer_2_out),
    .src1_addr(instruction_splitter_1_rs), .src2_addr(instruction_splitter_1_rt));
  Multiplexer #(.width(16), .enable("false")) multiplexer_4 (
    .in0(register_file_1_src2_data), .in1(Immediate), .out(multiplexer_4_out), .sel(AluSrc));
  ALU alu_1 (
    .A(register_file_1_src1_data), .B(multiplexer_4_out), .SHAMT(SHAMT), .OPCODE(ALUOp),
    .ALUResult(alu_1_aluresult), .CLK(CLK), .Zero(Zero));  // open: Cout, Overflow
  Multiplexer #(.width(16), .enable("false")) multiplexer_5 (
    .in0(alu_1_aluresult), .in1(ram_1_data), .out(multiplexer_5_out), .sel(MemtoReg));
  RAM #(.addrWidth(16), .dataWidth(16), .bus("separate")) ram_1 (
    .addr(alu_1_aluresult), .din(register_file_1_src2_data), .data(ram_1_data), .str(MemWrite), .clk(CLK),
    .ld(MemRead), .clr(button_2_out));  // open: sel
  Button button_2 (.out(button_2_out));

  // Notes on the sheet:
  //   Hakan Şahin - 64355 / Yasemin Melek - 63929
endmodule
